# Fritzing sketch CO2-Detect (saved by Fritzing 0.9.3b)
breadboards: 1

parts:
  Часть1 = Arduino Micro (Rev3)
  MH-Z14A = IC, DIP package, 20 pins [chip_label=MH-Z14A]
  U1 = 74HC595 [package="DIP16 [THT]"]
  U2 = 74HC595 [package="DIP16 [THT]"]
  LED2 = LED - 5mm [color="Red (633nm)" package="5 mm [THT]"]
  LED3 = LED - 5mm [color="Red (633nm)" package="5 mm [THT]"]
  LED4 = LED - 5mm [color="Red (633nm)" package="5 mm [THT]"]
  LED5 = LED - 5mm [color="Red (633nm)" package="5 mm [THT]"]
  LED23 = LED - 5mm [color="Red (633nm)" package="5 mm [THT]"]
  LED24 = LED - 5mm [color="Red (633nm)" package="5 mm [THT]"]
  LED25 = LED - 5mm [color="Red (633nm)" package="5 mm [THT]"]
  LED26 = LED - 5mm [color="Red (633nm)" package="5 mm [THT]"]
  LED27 = LED - 5mm [color="Red (633nm)" package="5 mm [THT]"]
  LED28 = LED - 5mm [color="Red (633nm)" package="5 mm [THT]"]
  LED29 = LED - 5mm [color="Red (633nm)" package="5 mm [THT]"]
  LED30 = LED - 5mm [color="Red (633nm)" package="5 mm [THT]"]
  LED31 = LED - 5mm [color="Red (633nm)" package="5 mm [THT]"]
  LED32 = LED - 5mm [color="Red (633nm)" package="5 mm [THT]"]
  LED33 = LED - 5mm [color="Red (633nm)" package="5 mm [THT]"]
  LED34 = LED - 5mm [color="Red (633nm)" package="5 mm [THT]"]
  LED35 = LED - 5mm [color="Red (633nm)" package="5 mm [THT]"]
  LED36 = LED - 5mm [color="Red (633nm)" package="5 mm [THT]"]
  R1 = Resistor [tolerance=±5% resistance=220 package=THT]
  R2 = Resistor [tolerance=±5% resistance=220 package=THT]
  R3 = Resistor [tolerance=±5% resistance=220 package=THT]
  R4 = Resistor [tolerance=±5% resistance=220 package=THT]
  R5 = Resistor [tolerance=±5% resistance=220 package=THT]
  R6 = Resistor [tolerance=±5% resistance=220 package=THT]
  R7 = Resistor [tolerance=±5% resistance=220 package=THT]
  R8 = Resistor [tolerance=±5% resistance=220 package=THT]
  R9 = Resistor [tolerance=±5% resistance=220 package=THT]
  R10 = Resistor [tolerance=±5% resistance=220 package=THT]
  R11 = Resistor [tolerance=±5% resistance=220 package=THT]
  R12 = Resistor [tolerance=±5% resistance=220 package=THT]
  R13 = Resistor [tolerance=±5% resistance=220 package=THT]
  R14 = Resistor [tolerance=±5% resistance=220 package=THT]
  R15 = Resistor [tolerance=±5% resistance=220 package=THT]
  R16 = Resistor [tolerance=±5% resistance=220 package=THT]
  R17 = Resistor [tolerance=±5% resistance=220 package=THT]
  R18 = Resistor [tolerance=±5% resistance=220 package=THT]
  SP1 = SPEAKER [package=pcb_mount_speaker]
  R19 = Resistor [tolerance=±5% resistance=220 package=THT]
  J1 = Screw terminal - 2 pins [package=THT]
  Часть2 = Adafruit BMP180
  Часть3 = TXB0108 8-channel Bi-directional Logic Level Converter
  LED37 = LED - 5mm [color="Red (633nm)" package="5 mm [THT]"]
  LED38 = LED - 5mm [color="Red (633nm)" package="5 mm [THT]"]
  LED39 = LED - 5mm [color="Red (633nm)" package="5 mm [THT]"]
  R20 = Resistor [tolerance=±5% resistance=220 package=THT]
  R21 = Resistor [tolerance=±5% resistance=220 package=THT]
  R22 = Resistor [tolerance=±5% resistance=220 package=THT]

nets:
  N1: Часть1.D1/TX, Часть3.B3
  N2: Часть1.D0/RX, Часть3.B4
  GND: Часть1.GND, MH-Z14A.pin2, SP1.-, J1.pin2, Часть2.GND, Часть3.GND
  N3: Часть1.D2/SDA, Часть2.SDA
  N4: Часть1.D3/SCL, Часть2.SCL
  N5: Часть1.D9_PWM/A9, U1.DS
  N6: Часть1.D10_PWM/A10, U1.ST_CP, U2.ST_CP
  N7: Часть1.D11_PWM, U1.SH_CP, U2.SH_CP
  N8: Часть1.D12_PWM/A11, U1.MR, U2.MR
  N9: Часть1.VIN, J1.pin1
  N10: Часть1.5V, MH-Z14A.pin1, Часть3.VCCB
  VCC: Часть1.3V3, U1.VCC, U2.VCC, Часть2.+3V3, Часть3.OE, Часть3.VCCA
  N11: Часть1.D13_PWM, R19.Pin_0
  N12: MH-Z14A.pin13, Часть3.A4
  N13: MH-Z14A.pin14, Часть3.A3
  GND_2: U1.GND, U1.OE, U2.GND, U2.OE
  N14: U1.Q7', U2.DS
  N15: U2.Q1, R4.Pin_1
  N16: U2.Q2, R3.Pin_1
  N17: U2.Q3, R6.Pin_1
  N18: U2.Q4, R5.Pin_1
  N19: U2.Q5, R8.Pin_1
  N20: U2.Q6, R7.Pin_1
  N21: U2.Q7, R18.Pin_1
  N22: U2.Q0, R1.Pin_1
  N23: LED2.anode, R5.Pin_0
  N24: LED3.anode, R8.Pin_0
  N25: LED4.anode, R7.Pin_0
  N26: LED5.anode, R18.Pin_0
  N27: LED23.anode, R6.Pin_0
  N28: LED24.anode, R4.Pin_0
  N29: LED25.anode, R3.Pin_0
  N30: LED26.anode, R2.Pin_0
  N31: LED27.anode, R1.Pin_0
  N32: LED28.anode, R9.Pin_0
  N33: LED29.anode, R16.Pin_0
  N34: LED30.anode, R14.Pin_0
  N35: LED31.anode, R15.Pin_0
  N36: LED32.anode, R12.Pin_0
  N37: LED33.anode, R13.Pin_0
  N38: LED34.anode, R10.Pin_0
  N39: LED35.anode, R17.Pin_0
  N40: LED36.anode, R11.Pin_0
  N41: SP1.+, R19.Pin_1
  N42: LED37.anode, R20.Pin_1
  N43: LED38.anode, R21.Pin_1
  N44: LED39.anode, R22.Pin_1

custom parts:
  Adafruit BMP180: This precision sensor from Bosch is the best low-cost sensing solution for measuring barometric pressure and temperature. Because pressure changes with altitude you can also use it as an altimeter! The sensor is soldered onto a PCB with a 3.3V regulator, I2C level shifter and pull-up resistors on the I2C pins. The BMP180 is the next-generation of sensors from Bosch, and replaces the BMP085.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
  TXB0108 8-channel Bi-directional Logic Level Converter: Because the Arduino (and Basic Stamp) are 5V devices, and most modern sensors, displays, flash cards and modes are 3.3V-only, many makers find that they need to perform level shifting/conversion to protect the 3.3V device from 5V. Although one can use resistors to make a divider, for high speed transfers, the resistors can add a lot of slew and cause havoc that is tough to debug. For that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
